// Logisim project Circuits.circ as structural Verilog
module halfAdder (
  input  inA,
  input  inB,
  output outS,
  output carryOut
);

  xor xor_1 (outS, inA, inB);
  and and_1 (carryOut, inA, inB);
endmodule

module fullAdder (
  input  carryIn,
  input  inA,
  input  inB,
  output outS,
  output carryOut
);

  wire halfadder_1_carryout, halfadder_1_outs, halfadder_2_carryout;

  halfAdder halfadder_1 (.inA(inA), .inB(inB), .outS(halfadder_1_outs), .carryOut(halfadder_1_carryout));
  halfAdder halfadder_2 (.inA(carryIn), .inB(halfadder_1_outs), .outS(outS), .carryOut(halfadder_2_carryout));
  or or_1 (carryOut, halfadder_2_carryout, halfadder_1_carryout);
endmodule

module adder4bit (
  input  c0,
  input  a0,
  input  b0,
  input  a1,
  input  b1,
  input  a2,
  input  b2,
  input  a3,
  input  b3,
  output s0,
  output s1,
  output s2,
  output s3,
  output overflow,
  output c4
);

  wire fulladder_1_carryout, fulladder_2_carryout, fulladder_3_carryout;

  fullAdder fulladder_1 (.carryIn(c0), .inA(a0), .inB(b0), .outS(s0), .carryOut(fulladder_1_carryout));
  fullAdder fulladder_2 (
    .carryIn(fulladder_1_carryout), .inA(a1), .inB(b1), .outS(s1), .carryOut(fulladder_2_carryout));
  fullAdder fulladder_3 (
    .carryIn(fulladder_2_carryout), .inA(a2), .inB(b2), .outS(s2), .carryOut(fulladder_3_carryout));
  fullAdder fulladder_4 (.carryIn(fulladder_3_carryout), .inA(a3), .inB(b3), .outS(s3), .carryOut(c4));
  xor xor_1 (overflow, fulladder_3_carryout, c4);
endmodule

module mux1bit (
  input  A,
  input  B,
  input  opCode,
  output out_4
);

  wire and_1_out, and_2_out, not_1_out;

  not not_1 (not_1_out, opCode);
  and and_1 (and_1_out, A, not_1_out);
  and and_2 (and_2_out, opCode, B);
  or or_1 (out_4, and_1_out, and_2_out);
endmodule

module mux4bit (
  input  a,
  input  b,
  input  c,
  input  d,
  input  op1,
  input  op2
);

  wire and_1_out, and_2_out, and_3_out, and_4_out, not_1_out, not_2_out;

  not not_1 (not_1_out, d);
  not not_2 (not_2_out, op1);
  and and_1 (and_1_out, d, not_2_out, d);
  and and_2 (and_2_out, a, not_2_out, not_1_out);
  and and_3 (and_3_out, b, not_2_out, d);
  and and_4 (and_4_out, c, op1, not_1_out);
  // OR_Gate or_1 has open pins: in0=and_2_out, in1=and_3_out, in2=and_4_out, in3=and_1_out, out=open

  assign op2 = d;
endmodule

module ula1bit (
);

  mux1bit mux1bit_1 ();  // open: A, B, opCode, out_4
  mux4bit mux4bit_1 ();  // open: a, b, c, d, op1, op2
  // OR_Gate or_1 is placed but not wired
  // AND_Gate and_1 is placed but not wired
  // NOT_Gate not_1 is placed but not wired
  fullAdder fulladder_1 ();  // open: carryIn, inA, inB, outS, carryOut
endmodule

module _74181Circuit (
  input  [3:0] A,
  input  [3:0] B,
  input  [3:0] in_3,
  output [3:0] out_4
);

  wire [3:0] and_1_out, and_2_out, and_3_out, nand_1_out, nor_1_out, not_1_out, not_2_out, or_1_out,
       or_2_out, or_3_out, xnor_1_out, xor_1_out;

  assign not_1_out = ~A;  // NOT_Gate not_1, 4 bits wide
  assign nor_1_out = ~(A | B);  // NOR_Gate nor_1, 4 bits wide
  assign and_1_out = ~A & B;  // AND_Gate and_1, 4 bits wide
  assign nand_1_out = ~(A & B);  // NAND_Gate nand_1, 4 bits wide
  assign not_2_out = ~B;  // NOT_Gate not_2, 4 bits wide
  assign xor_1_out = A ^ B;  // XOR_Gate xor_1, 4 bits wide
  assign and_2_out = A & ~B;  // AND_Gate and_2, 4 bits wide
  assign or_1_out = ~A | B;  // OR_Gate or_1, 4 bits wide
  assign xnor_1_out = ~(A ^ B);  // XNOR_Gate xnor_1, 4 bits wide
  assign and_3_out = A & B;  // AND_Gate and_3, 4 bits wide
  assign or_2_out = A | ~B;  // OR_Gate or_2, 4 bits wide
  assign or_3_out = A | B;  // OR_Gate or_3, 4 bits wide
  Multiplexer #(.select(4), .width(4), .disabled(0)) multiplexer_1 (
    .in0(not_1_out), .in1(nor_1_out), .in2(and_1_out), .in3(4'b0000), .in4(nand_1_out), .in5(not_2_out),
    .in6(xor_1_out), .in7(and_2_out), .in8(or_1_out), .in9(xnor_1_out), .in10(A), .in11(and_3_out),
    .in12(4'b1111), .in13(or_2_out), .in14(or_3_out), .in15(A), .out(out_4), .sel(in_3));  // open: en
endmodule
