// Logisim project Adders.circ as structural Verilog: 3 circuits, main circuit halfAdder
module halfAdder (
  input  inA,
  input  inB,
  output outS,
  output carryOut
);

  xor xor_1 (outS, inA, inB);
  and and_1 (carryOut, inA, inB);
endmodule

module fullAdder (
  input  carryIn,
  input  inA,
  input  inB,
  output outS,
  output carryOut
);

  wire halfadder_1_carryout, halfadder_1_outs, halfadder_2_carryout;

  halfAdder halfadder_1 (.inA(inA), .inB(inB), .outS(halfadder_1_outs), .carryOut(halfadder_1_carryout));
  halfAdder halfadder_2 (.inA(carryIn), .inB(halfadder_1_outs), .outS(outS), .carryOut(halfadder_2_carryout));
  or or_1 (carryOut, halfadder_2_carryout, halfadder_1_carryout);
endmodule

module adder4bit (
  input  c0,
  input  a0,
  input  b0,
  input  a1,
  input  b1,
  input  a2,
  input  b2,
  input  a3,
  input  b3,
  output s0,
  output s1,
  output s2,
  output s3,
  output overflow,
  output c4
);

  wire fulladder_1_carryout, fulladder_2_carryout, fulladder_3_carryout;

  fullAdder fulladder_1 (.carryIn(c0), .inA(a0), .inB(b0), .outS(s0), .carryOut(fulladder_1_carryout));
  fullAdder fulladder_2 (
    .carryIn(fulladder_1_carryout), .inA(a1), .inB(b1), .outS(s1), .carryOut(fulladder_2_carryout));
  fullAdder fulladder_3 (
    .carryIn(fulladder_2_carryout), .inA(a2), .inB(b2), .outS(s2), .carryOut(fulladder_3_carryout));
  fullAdder fulladder_4 (.carryIn(fulladder_3_carryout), .inA(a3), .inB(b3), .outS(s3), .carryOut(c4));
  xor xor_1 (overflow, fulladder_3_carryout, c4);
endmodule
